# Fritzing sketch ifridge_idorsia_1 (saved by Fritzing 0.9.3b)
breadboards: 1

parts:
  Pololu_A1 = Pololu A4988 [package=SO16]
  M1 = Stepper Motor - Bipolar
  Pololu_A2 = Pololu A4988 [package=SO16]
  M2 = Stepper Motor - Bipolar
  5V_(Ardunio_&_Raspberry) = LM2596 step down module
  Nano = Arduino Nano v2.3
  S1_Open = Round Pushbutton
  12-24V_(motors)_-_To_be_sure = LM2596 step down module
  Power_Supply_12-24V = DC Power [voltage=5]
  R1_Pullup = Resistor [tolerance=±5% resistance=10k package=THT]
  R3_limit_current = Resistor [tolerance=±5% resistance=1k package=THT]
  C1_debounce_capacitor = Ceramic Capacitor [capacitance=10µF package="100 mil [THT, multilayer]"]
  R4_limit_current = Resistor [tolerance=±5% resistance=1k package=THT]
  S2_Close = Round Pushbutton
  C2_debounce_capacitor = Ceramic Capacitor [capacitance=10µF package="100 mil [THT, multilayer]"]
  Proximity_Open = Infrared Proximity Sensor
  Proximity_Close = Infrared Proximity Sensor
  R2_Pullup = Resistor [tolerance=±5% resistance=10k package=THT]
  MCU1 = Raspberry Pi Zero
  Part1 = Adafruit 128x64 OLED Bonnet [part_number="Adafruit #3531"]

nets:
  N1: Pololu_A1.ENABLE, Pololu_A2.ENABLE, Nano.D10
  N2: Pololu_A1.RESET, Pololu_A1.SLEEP
  N3: Pololu_A1.STEP, Nano.D6
  N4: Pololu_A1.DIR, Nano.D4
  GND: Pololu_A1.GND, Pololu_A2.GND, 5V_(Ardunio_&_Raspberry).IN-, 5V_(Ardunio_&_Raspberry).OUT-, S1_Open.leg0, 12-24V_(motors)_-_To_be_sure.IN-, 12-24V_(motors)_-_To_be_sure.OUT-, Power_Supply_12-24V.V-, C1_debounce_capacitor.0, C2_debounce_capacitor.0, Proximity_Open.GND, Proximity_Close.GND, MCU1.pin_6, MCU1.pin_25
  VDD: Pololu_A1.VDD, Pololu_A2.VDD, R1_Pullup.Pin_0, Proximity_Open.Vcc, Proximity_Close.Vcc
  N5: Pololu_A1.1B, M1.D
  N6: Pololu_A1.1A, M1.B
  N7: Pololu_A1.2A, M1.C
  N8: Pololu_A1.2B, M1.A
  N9: Pololu_A1.VMOT, Pololu_A2.VMOT, Nano.GND, 12-24V_(motors)_-_To_be_sure.OUT+
  N10: Pololu_A2.RESET, Pololu_A2.SLEEP
  N11: Pololu_A2.STEP, Nano.D5
  N12: Pololu_A2.DIR, Nano.D8
  N13: Pololu_A2.1B, M2.D
  N14: Pololu_A2.1A, M2.B
  N15: Pololu_A2.2A, M2.C
  N16: Pololu_A2.2B, M2.A
  N17: 5V_(Ardunio_&_Raspberry).IN+, 12-24V_(motors)_-_To_be_sure.IN+, Power_Supply_12-24V.V+, MCU1.pin_2, MCU1.pin_4
  N18: 5V_(Ardunio_&_Raspberry).OUT+, Nano.VIN
  N19: Nano.D11, R4_limit_current.Pin_0
  N20: Nano.D12, R3_limit_current.Pin_0
  N21: Nano.A5, MCU1.pin_5, Part1.SCL
  N22: Nano.A4, MCU1.pin_3, Part1.SDA
  N23: Nano.A1, Proximity_Close.Vout
  N24: Nano.A0, Proximity_Open.Vout
  N25: Nano.+5V, R2_Pullup.Pin_0
  N26: S1_Open.leg1, R1_Pullup.Pin_1, R3_limit_current.Pin_1, C1_debounce_capacitor.1
  N27: R4_limit_current.Pin_1, S2_Close.leg1, C2_debounce_capacitor.1, R2_Pullup.Pin_1

custom parts:
  LM2596 step down module: LM2596 DC-DC step down power supply module 3 A.
  Adafruit 128x64 OLED Bonnet: If you'd like a compact display, with buttons and a joystick - we've got what you're looking for. The Adafruit 128x64 OLED Bonnet for Raspberry Pi is the big sister to our mini PiOLED add-on. This version has 128x64 pixels (instead of 128x32) and a much larger screen besides. With the OLED display in the center, we had some space on either side so we added a 5-way joystick and two pushbuttons.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
